# Fritzing sketch sketch (saved by Fritzing 0.9.3b)

parts:
  Composant1 = Arduino Leonardo (Rev3b)
  startButton = Pushbutton [package="[THT]"]
  actionButton = Pushbutton [package="[THT]"]

nets:
  N1: Composant1.D2/SDA, Composant1.SDA, startButton.Pin_1
  N2: Composant1.D3_PWM/SCL, actionButton.Pin_1
  N3: Composant1.GND, startButton.Pin_3, actionButton.Pin_3
